# Fritzing sketch arduino+driver+motors+ir (saved by Fritzing 0.8.7b)
breadboards: 1

parts:
  IC1 = L293D [package=THT]
  M1 = DC Motor
  M2 = DC Motor
  Part1 = Arduino Uno (Rev3)
  IR1 = TSOP312.., 314.. [package=THT]

nets (from the schematic view):
  N1: IC1.Enable_1, IC1.+Vmotor, IC1.Enable_2, IC1.+V, Part1.5V, IR1.Vs
  N2: IC1.In_1, Part1.D12/MISO
  N3: IC1.Out_1_(_Controlled_by_Enable_1_), M2.pin_2
  GND: IC1.0V, Part1.GND, IR1.GND
  N4: IC1.Out_2_(_Controlled_by_Enable_1_), M2.pin_1
  N5: IC1.In_2, Part1.D11_PWM/MOSI
  N6: IC1.In_3, Part1.D9_PWM
  N7: IC1.Out_3_(_Controlled_by_Enable_2_), M1.pin_1
  N8: IC1.Out_4_(_Controlled_by_Enable_2_), M1.pin_2
  N9: IC1.In_4, Part1.D10_PWM/SS
  N10: Part1.D2, IR1.Data
