# Fritzing sketch arduino+driver+motors (saved by Fritzing 0.9.1b)
breadboards: 1

parts:
  IC1 = L293D [package=THT]
  Motor_2 = DC Motor
  Motor_1 = DC Motor
  Part1 = Arduino Uno (Rev3)

nets:
  N1: IC1.Enable_1, IC1.+Vmotor, IC1.Enable_2, IC1.+V, Part1.5V
  N2: IC1.In_1, Part1.D12/MISO
  N3: IC1.Out_1_(_Controlled_by_Enable_1_), Motor_1.pin_2
  N4: IC1.0V, Part1.GND
  N5: IC1.Out_2_(_Controlled_by_Enable_1_), Motor_1.pin_1
  N6: IC1.In_2, Part1.D11_PWM/MOSI
  N7: IC1.In_3, Part1.D9_PWM
  N8: IC1.Out_3_(_Controlled_by_Enable_2_), Motor_2.pin_1
  N9: IC1.Out_4_(_Controlled_by_Enable_2_), Motor_2.pin_2
  N10: IC1.In_4, Part1.D10_PWM/SS
