# Fritzing sketch single-motor-circuit-schematic (saved by Fritzing 0.8.7b)
breadboards: 1

parts:
  M1 = DC Motor
  S1 = SPST Switch [package=switche-dpdt]
  S2 = SPST Switch [package=switche-dpdt]

nets:
  N1: M1.pin_1, S1.P
  N2: M1.pin_2, S2.P
  5V: S1.O, S2.O
  GND: S1.S, S2.S
